// Logisim project ula4_CORE.circ as structural Verilog: 7 circuits, main circuit ula4_nucleo
module ula4_nucleo (
  input  [3:0] A,
  input  [3:0] B,
  input  [2:0] OP,
  output [7:0] F,
  output C,
  output V,
  output Z
);

  ula4_z_detect8_v1 ula4_z_detect8_v1_1 (
    .in_1(A[0]), .in_2(A[1]), .in_3(A[2]), .in_4(A[3]), .in_5(B[0]), .in_6(B[1]), .in_7(B[2]), .in_8(B[3]),
    .out_9(Z));

  assign F = {B, A};
endmodule

module ula4_z_detect8_v1 (
  input  in_1,
  input  in_2,
  input  in_3,
  input  in_4,
  input  in_5,
  input  in_6,
  input  in_7,
  input  in_8,
  output out_9
);

  wire logic4_nor_1_out_3, logic4_nor_2_out_3, logic4_nor_3_out_3, logic4_nor_4_out_3, logic4_nor_5_out_3,
       logic4_nor_6_out_3, not_1_out, not_2_out, not_3_out, not_4_out, not_5_out, not_6_out;

  logic4_nor logic4_nor_1 (.in_1(in_1), .in_2(in_2), .out_3(logic4_nor_1_out_3));
  not not_1 (not_1_out, logic4_nor_1_out_3);
  logic4_nor logic4_nor_2 (.in_1(not_1_out), .in_2(in_3), .out_3(logic4_nor_2_out_3));
  not not_2 (not_2_out, logic4_nor_2_out_3);
  logic4_nor logic4_nor_3 (.in_1(not_2_out), .in_2(in_4), .out_3(logic4_nor_3_out_3));
  not not_3 (not_3_out, logic4_nor_3_out_3);
  logic4_nor logic4_nor_4 (.in_1(not_3_out), .in_2(in_5), .out_3(logic4_nor_4_out_3));
  not not_4 (not_4_out, logic4_nor_4_out_3);
  not not_5 (not_5_out, logic4_nor_5_out_3);
  logic4_nor logic4_nor_5 (.in_1(not_4_out), .in_2(in_6), .out_3(logic4_nor_5_out_3));
  not not_6 (not_6_out, logic4_nor_6_out_3);
  logic4_nor logic4_nor_6 (.in_1(not_5_out), .in_2(in_7), .out_3(logic4_nor_6_out_3));
  logic4_nor logic4_nor_7 (.in_1(not_6_out), .in_2(in_8), .out_3(out_9));
endmodule

module logic4_xor (
  input  in_1,
  input  in_2,
  output out_3
);

  wire and_1_out, and_2_out, not_1_out, not_2_out;

  not not_1 (not_1_out, in_2);
  not not_2 (not_2_out, in_1);
  and and_1 (and_1_out, in_1, not_1_out);
  and and_2 (and_2_out, not_2_out, in_2);
  or or_1 (out_3, and_1_out, and_2_out);
endmodule

module logic4_nand (
  input  in_1,
  input  in_2,
  output out_3
);

  wire and_1_out;

  and and_1 (and_1_out, in_1, in_2);
  not not_1 (out_3, and_1_out);
endmodule

module logic4_nor (
  input  in_1,
  input  in_2,
  output out_3
);

  wire or_1_out;

  or or_1 (or_1_out, in_1, in_2);
  not not_1 (out_3, or_1_out);
endmodule

module codes4_bin2gray4 (
  input  in_1,
  input  in_2,
  input  in_3,
  input  in_4,
  output out_5,
  output out_6,
  output out_7,
  output out_8
);

  logic4_xor logic4_xor_1 (.in_1(in_1), .in_2(in_2), .out_3(out_6));
  logic4_xor logic4_xor_2 (.in_1(in_2), .in_2(in_3), .out_3(out_7));
  logic4_xor logic4_xor_3 (.in_1(in_3), .in_2(in_4), .out_3(out_8));

  assign out_5 = in_1;
endmodule

module codes4_parity8_gen_check (
  input  in_1,
  input  in_2,
  input  in_3,
  input  in_4,
  input  in_5,
  input  in_6,
  input  in_7,
  input  in_8,
  output out_9
);

  wire logic4_xor_1_out_3, logic4_xor_2_out_3, logic4_xor_3_out_3, logic4_xor_4_out_3, logic4_xor_5_out_3,
       logic4_xor_6_out_3;

  logic4_xor logic4_xor_1 (.in_1(in_1), .in_2(in_2), .out_3(logic4_xor_1_out_3));
  logic4_xor logic4_xor_2 (.in_1(logic4_xor_1_out_3), .in_2(in_3), .out_3(logic4_xor_2_out_3));
  logic4_xor logic4_xor_3 (.in_1(logic4_xor_2_out_3), .in_2(in_4), .out_3(logic4_xor_3_out_3));
  logic4_xor logic4_xor_4 (.in_1(logic4_xor_3_out_3), .in_2(in_5), .out_3(logic4_xor_4_out_3));
  logic4_xor logic4_xor_5 (.in_1(logic4_xor_4_out_3), .in_2(in_6), .out_3(logic4_xor_5_out_3));
  logic4_xor logic4_xor_6 (.in_1(logic4_xor_5_out_3), .in_2(in_7), .out_3(logic4_xor_6_out_3));
  logic4_xor logic4_xor_7 (.in_1(logic4_xor_6_out_3), .in_2(in_8), .out_3(out_9));
endmodule
